# Fritzing sketch TransmitterCircuit (saved by Fritzing 0.9.3b)

parts:
  Part1 = Thumb Joystick
  Part2 = Arduino Nano (Rev3.0)
  Part3 = Thumb Joystick
  Part4 = NRF24L01+ Breakout Board

nets:
  GND: Part1.GND, Part2.GND, Part3.GND, Part4.GND
  N1: Part1.HORZ, Part2.A1
  N2: Part1.VERT, Part2.A0
  VCC: Part1.VCC, Part2.5V, Part3.VCC
  N3: Part2.D9, Part4.CE
  N4: Part2.D10, Part4.CS
  N5: Part2.D11/MOSI, Part4.MOSI
  N6: Part2.D12/MISO, Part4.MISO
  N7: Part2.A3, Part3.HORZ
  N8: Part2.A2, Part3.VERT
  3V3: Part2.3V3, Part4.VCC
  N9: Part2.D13/SCK, Part4.SCK

notes:
  4-Channel Rover Transmitter
  ~Nishant Rana
